# Fritzing sketch Bubbles (saved by Fritzing 0.9.4)
circuit board: 10cm x 8cm

parts:
  5v_Power = Camdenboss CTB0158-2 [part_number=CTB0158-2 package=THT]
  R1 = Resistor [tolerance=±5% resistance=220 package=THT]
  R2 = Resistor [tolerance=±5% resistance=100 package=THT]
  R3 = Resistor [tolerance=±5% resistance=10k package=THT]
  3_3v_Relay = OMRON PCB Power Relay – G5LE [part_number="G5LE-1\r\n" package=THT]
  Relay_Out = Camdenboss CTB0158-3 [part_number=CTB0158-3 package=THT]
  Status = LED - 3mm [color="Red (633nm)" package="3 mm [THT]"]
  Power = LED - 3mm [color="Red (633nm)" package="3 mm [THT]"]
  Pwr = SPST Switch [package=switch-spdt]
  3v_<->_5v = Logic Level Converter
  5v_Logic = Camdenboss CTB0158-4 [part_number=CTB0158-4 package=THT]
  J1 = Camdenboss CTB0158-8 [part_number=CTB0158-8 package=THT]
  Input = Momentary Switch [package=ksa_sealed_tac_switch]
  J2 = Camdenboss CTB0158-8 [part_number=CTB0158-8 package=THT]
  IC = WeMos D1 Mini

nets:
  N1: 5v_Power.pin1, Pwr.P
  N2: 5v_Power.pin2, R3.Pin_0, 3_3v_Relay.COIL1, Status.cathode, Power.cathode, 3v_<->_5v.GND, J2.pin7, IC.G
  N3: R1.Pin_0, Power.anode
  N4: R1.Pin_1, Pwr.S, 3v_<->_5v.HV, J2.pin8, IC.5V
  N5: R2.Pin_0, Status.anode
  N6: R2.Pin_1, J2.pin5, IC.D3
  N7: R3.Pin_1, Input.1
  N8: 3_3v_Relay.A, Relay_Out.pin3
  N9: 3_3v_Relay.C, Relay_Out.pin2
  N10: 3_3v_Relay.COIL2, 3v_<->_5v.TX2_LV, J1.pin4, IC.D5
  N11: 3_3v_Relay.B, Relay_Out.pin1
  N12: 3v_<->_5v.RX2_LV, J1.pin5, IC.D6
  N13: 3v_<->_5v.LV, J1.pin8, Input.4, IC.3V3
  N14: 3v_<->_5v.RX_LV, J1.pin6, IC.D7
  N15: 3v_<->_5v.TX_LV, J1.pin7, IC.D8
  N16: 3v_<->_5v.TX_HV, 5v_Logic.pin1
  N17: 3v_<->_5v.RX_HV, 5v_Logic.pin2
  N18: 3v_<->_5v.RX2_HV, 5v_Logic.pin3
  N19: 3v_<->_5v.TX2_HV, 5v_Logic.pin4
  N20: J1.pin1, IC.RST
  N21: J1.pin2, IC.A0
  N22: J1.pin3, IC.D0
  N23: Input.3, J2.pin6, IC.D4
  N24: J2.pin1, IC.TX
  N25: J2.pin2, IC.RX
  N26: J2.pin3, IC.D1
  N27: J2.pin4, IC.D2

notes:
  3v D8 D7 D6 D5 D0 A0 RST
  5v G  D4 D3 D2 D1 RX TX
  |_  \  _|
  TX1 RX1 TX0 RX0
  bubbles
  G 5v
  JLCJLCJLCJLC
  v0.1-15.07.20
  O   |
  0.1

custom parts:
  WeMos D1 Mini: The D1 mini is a mini wifi board based on ESP-8266EX.
